# Fritzing sketch P13_00_00-Main (saved by Fritzing 0.9.3b)
breadboards: 1

parts:
  U3 = RELAY-2 [package=relay-g5v]
  U4 = RELAY-2 [package=relay-g5v]
  Q2 = NPN-Transistor [package="TO92 [THT]"]
  Q3 = NPN-Transistor [package="TO92 [THT]"]
  D1 = Rectifier Diode [part_number=1N4001 package="300 mil [THT]"]  # not connected
  R1 = Resistor [tolerance=±5% resistance=10 package=THT]
  R2 = Resistor [tolerance=±5% resistance=10 package=THT]
  R3 = Resistor [tolerance=±5% resistance=150 package=THT]
  R4 = Resistor [tolerance=±5% resistance=1k package=THT]
  LED1 = LED - 5mm [color="Red (633nm)" package="5 mm [THT]"]
  U5 = attiny85 [package=dip]
  U6 = Voltage Regulator [package=to220-adj]
  C1 = Electrolytic Capacitor [capacitance=1µF package="100 mil [THT, electrolytic]"]
  R5 = Resistor [tolerance=±5% resistance=1k package=THT]
  LED2 = LED - 5mm [color="Red (633nm)" package="5 mm [THT]"]
  R6 = Resistor [tolerance=±5% resistance=10 package=THT]
  D2 = Rectifier Diode [part_number=1N4001 package="300 mil [THT]"]
  R7 = Resistor [tolerance=±5% resistance=10 package=THT]
  R8 = Resistor [tolerance=±5% resistance=150 package=THT]
  R9 = Resistor [tolerance=±5% resistance=1k package=THT]
  LED3 = LED - 5mm [color="Red (633nm)" package="5 mm [THT]"]
  U7 = RELAY-2 [package=relay-g5v]
  D3 = Rectifier Diode [part_number=1N4001 package="300 mil [THT]"]
  Q4 = NPN-Transistor [package="TO92 [THT]"]
  R10 = Resistor [tolerance=±5% resistance=150 package=THT]
  R11 = Resistor [tolerance=±5% resistance=10 package=THT]
  R12 = Resistor [tolerance=±5% resistance=10 package=THT]
  S1 = Pushbutton [package="[THT]"]
  R13 = Resistor [tolerance=±5% resistance=1k package=THT]
  Power_plug1 = Power plug
  R14 = Resistor [tolerance=±5% resistance=1k package=THT]
  LED4 = LED - 5mm [color="Red (633nm)" package="5 mm [THT]"]

nets:
  N1: U3.1, Q3.C, D2.anode
  N2: U3.2, R6.Pin_1
  N3: U3.6, U4.5, U4.6, Q2.E, Q3.E, U5.Pin_4, U6.IN, C1.-, U7.5, U7.6, Q4.E, R13.Pin_1, Power_plug1.GND, LED4.cathode
  N4: U3.9, R7.Pin_0
  N5: U3.10, D2.cathode, R8.Pin_0
  N6: U4.1, Q2.C
  N7: U4.2, R1.Pin_1
  N8: U4.9, R2.Pin_0
  N9: U4.10, R3.Pin_0
  N10: Q2.B, LED1.cathode
  N11: Q3.B, LED2.cathode
  N12: R1.Pin_0, R2.Pin_1, R3.Pin_1, U6.ADJ, R6.Pin_0, R7.Pin_1, R8.Pin_1, R10.Pin_1, R11.Pin_1, R12.Pin_0, Power_plug1.VCC
  N13: R4.Pin_0, LED1.anode
  N14: R4.Pin_1, U5.Pin_5
  N15: U5.Pin_2, R14.Pin_1
  N16: U5.Pin_3, S1.Pin_3, S1.Pin_4, R13.Pin_0
  N17: U5.Pin_6, R5.Pin_1
  N18: U5.Pin_7, R9.Pin_1
  N19: U5.Pin_8, U6.OUT, C1.+, S1.Pin_1, S1.Pin_2
  N20: R5.Pin_0, LED2.anode
  N21: R9.Pin_0, LED3.anode
  N22: LED3.cathode, Q4.B
  N23: U7.1, D3.anode, Q4.C
  N24: U7.2, R12.Pin_1
  N25: U7.9, R11.Pin_0
  N26: U7.10, D3.cathode, R10.Pin_0
  N27: R14.Pin_0, LED4.anode
